# Fritzing sketch Capstone (saved by Fritzing 0.9.4)
breadboards: 1

parts:
  OLED_I2C1 = OLED 128x64 I2C Monochrome Display
  M1 = BMP280
  MAX30102_Sensor1 = MAX30102 Oximeter and Heart-Rate Sensor [part_number=MAX30102]
  Argon1 = Particle Argon
  S1 = Pushbutton [package="[THT]"]
  R1 = Resistor [tolerance=±5% resistance=100 package="0402 [SMD]"]
  GY1 = MPU-6050 Board GY-521 [form="♀ (female)" package=THT]

nets:
  N1: OLED_I2C1.SDA, M1.SDA, MAX30102_Sensor1.SDA, Argon1.SDA, GY1.pin4
  N2: OLED_I2C1.SCK, M1.SCL, MAX30102_Sensor1.SCL, Argon1.SCL, GY1.pin3
  VIN: OLED_I2C1.VDD, M1.VIN, MAX30102_Sensor1.VIN, Argon1.3.3V, S1.Pin_3, S1.Pin_4, GY1.pin1
  GND: OLED_I2C1.GND, M1.GND, MAX30102_Sensor1.GND, Argon1.GND, R1.Pin_1, GY1.pin2
  N3: Argon1.D2, S1.Pin_1, S1.Pin_2, R1.Pin_0

custom parts:
  BMP280: Temperature Humidity Barometric presure Sensor, I2C
  MAX30102 Oximeter and Heart-Rate Sensor: The MAX30102 is an integrated pulse oximetry and heart-rate monitor biosensor module. It includes internal LEDs, photodetectors, optical elements, and low-noise electronics with ambient light rejection. The MAX30102 operates on a single 1.8V power supply and a separate 3.3V power supply for the internal LEDs. Communication is through a I2C-compatible interface.
  Particle Argon: The Argon is a powerful Wi-Fi enabled development board that can act as either a standalone Wi-Fi endpoint or Wi-Fi enabled gateway for Particle Mesh networks. It is based on the Nordic nRF52840 and has built-in battery charging circuitry so it’s easy to connect a Li-Po and deploy your local network in minutes. The Argon is great for connecting existing projects to the Particle Device Cloud or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
  Pushbutton: A generic pushbutton.
  MPU-6050 Board GY-521: Acelerometro y Giroscopio MPU-6050 Board GY-521
